# Fritzing sketch Build Light (saved by Fritzing 0.9.2b)
circuit board: 4.78941cm x 3.93513cm
breadboards: 1

parts:
  PNP = PNP-Transistor [package="TO92 [THT]"]
  R2 = Resistor [tolerance=±1% resistance=220 package=THT]
  NPN = NPN-Transistor [package="TO92 [THT]"]
  R3 = Resistor [tolerance=±1% resistance=470 package=THT]
  PNP_2 = PNP-Transistor [package="TO92 [THT]"]
  R4 = Resistor [tolerance=±1% resistance=220 package=THT]
  R5 = Resistor [tolerance=±1% resistance=220 package=THT]
  NPN_2 = NPN-Transistor [package="TO92 [THT]"]
  R6 = Resistor [tolerance=±1% resistance=470 package=THT]
  PNP_3 = PNP-Transistor [package="TO92 [THT]"]
  R7 = Resistor [tolerance=±1% resistance=220 package=THT]
  R8 = Resistor [tolerance=±1% resistance=220 package=THT]
  NPN_3 = NPN-Transistor [package="TO92 [THT]"]
  R9 = Resistor [tolerance=±1% resistance=470 package=THT]
  RED = female pin header, 3 pins [form="♀ (female)"]
  GREEN = female pin header, 3 pins [form="♀ (female)"]
  R1 = Resistor [tolerance=±1% resistance=220 package=THT]
  YELLOW = female pin header, 3 pins [form="♀ (female)"]
  Part1 = Photon

nets:
  N1: PNP.E, R2.Pin_0, PNP_2.E, R5.Pin_0, PNP_3.E, R8.Pin_0, RED.pin3, GREEN.pin3, YELLOW.pin3, Part1.VIN
  N2: PNP.B, R1.Pin_0
  N3: PNP.C, RED.pin2
  N4: R2.Pin_1, NPN.C, R1.Pin_1
  N5: NPN.E, NPN_2.E, NPN_3.E, RED.pin1, GREEN.pin1, YELLOW.pin1, Part1.GND
  N6: NPN.B, R3.Pin_0
  N7: R3.Pin_1, Part1.D0
  N8: PNP_2.B, R4.Pin_0
  N9: PNP_2.C, YELLOW.pin2
  N10: R4.Pin_1, R5.Pin_1, NPN_2.C
  N11: NPN_2.B, R6.Pin_0
  N12: R6.Pin_1, Part1.D3
  N13: PNP_3.B, R7.Pin_0
  N14: PNP_3.C, GREEN.pin2
  N15: R7.Pin_1, R8.Pin_1, NPN_3.C
  N16: NPN_3.B, R9.Pin_0
  N17: R9.Pin_1, Part1.D6

notes:
  Red relay signal
  +
  Build Light 1.0

custom parts:
  Photon: The Photon is a tiny Wi-Fi development board that makes it easy to create internet-connected hardware. The Photon is all you need to get started. Power it over USB and in minutes you'll be controlling LEDs, switches, and motors and collecting data from sensors over the internet! It has 18 digital I/O pins, 8 analog input pins, 2 analog outputs (DAC), 9 PWM pins; UART (Serial), SPI, I2S, I2C,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
